# Fritzing sketch biotix_example (saved by Fritzing 0.9.0b)
breadboards: 1

parts:
  Part1 = Arduino Uno (Rev3)
  R1 = Rotary Potentiometer (Small) [maximum_resistance=100kΩ package=THT]
  R2 = Photocell (LDR) [package=THT]
  R3 = Resistor [tolerance=±5% resistance=220 package=THT]

nets:
  N1: Part1.A0, R1.wiper
  N2: Part1.A1, R2.pin_1, R3.Pin_0
  N3: Part1.5V, R1.leg2, R2.pin_0
  N4: Part1.GND, R1.leg1, R3.Pin_1

notes:
  potentiometer
  light sensitive resistor
